// Logisim project MAPADDER4.circ as structural Verilog: 3 circuits, main circuit adder1
module adder1 (
  input  A,
  input  B,
  output S,
  output C
);

  xor xor_1 (S, A, B);
  and and_1 (C, B, A);
endmodule

module adder1_full (
  input  Cin,
  input  A,
  input  B,
  output S,
  output Cout
);

  wire adder1_1_c, adder1_2_c, adder1_2_s;

  adder1 adder1_2 (.A(A), .B(B), .S(adder1_2_s), .C(adder1_2_c));
  adder1 adder1_1 (.A(Cin), .B(adder1_2_s), .S(S), .C(adder1_1_c));
  or or_1 (Cout, adder1_1_c, adder1_2_c);
endmodule

module adder4 (
  input  A0,
  input  B0,
  input  Cin,
  input  A1,
  input  B1,
  input  A2,
  input  B2,
  input  A3,
  input  B3,
  output S0,
  output S1,
  output S2,
  output S3,
  output Cout
);

  wire adder1_full_1_cout, adder1_full_2_cout, adder1_full_3_cout;

  adder1_full adder1_full_1 (.Cin(A0), .A(B0), .B(Cin), .S(S0), .Cout(adder1_full_1_cout));
  adder1_full adder1_full_2 (.Cin(adder1_full_1_cout), .A(A1), .B(B1), .S(S1), .Cout(adder1_full_2_cout));
  adder1_full adder1_full_3 (.Cin(adder1_full_2_cout), .A(A2), .B(B2), .S(S2), .Cout(adder1_full_3_cout));
  adder1_full adder1_full_4 (.Cin(adder1_full_3_cout), .A(A3), .B(B3), .S(S3), .Cout(Cout));
endmodule
