// Logisim project dekoder.circ as structural Verilog: 5 circuits, main circuit sseg
module sseg (
  input  d,
  input  c,
  input  b,
  input  a,
  output sa,
  output sb,
  output sc,
  output sd,
  output se,
  output sf,
  output sg
);

  wire and_1_out, and_2_out, and_3_out, and_4_out, and_5_out, and_6_out, and_7_out, and_8_out, and_9_out,
       and_10_out, and_11_out, and_12_out, and_13_out, and_14_out, and_15_out, and_16_out, and_17_out,
       and_18_out, and_19_out, and_20_out, and_21_out, and_22_out, and_23_out, not_1_out, not_2_out,
       not_3_out, not_4_out;

  not not_1 (not_1_out, d);
  not not_2 (not_2_out, c);
  not not_3 (not_3_out, b);
  not not_4 (not_4_out, a);
  and and_1 (and_1_out, not_3_out, c, a);
  and and_2 (and_2_out, not_3_out, d);
  and and_3 (and_3_out, not_4_out, not_3_out, not_2_out);
  and and_4 (and_4_out, b, not_1_out);
  and and_5 (and_5_out, not_4_out, not_3_out);
  and and_6 (and_6_out, a, b, not_1_out);
  and and_7 (and_7_out, c, not_1_out);
  and and_8 (and_8_out, a, b, not_2_out);
  and and_9 (and_9_out, not_4_out, b);
  and and_10 (and_10_out, not_4_out, not_3_out, not_2_out);
  and and_11 (and_11_out, not_2_out, d);
  and and_12 (and_12_out, a, not_3_out, c);
  and and_13 (and_13_out, b, not_2_out);
  and and_14 (and_14_out, not_4_out, b);
  and and_15 (and_15_out, not_4_out, not_3_out, not_2_out);
  and and_16 (and_16_out, not_4_out, not_3_out);
  and and_17 (and_17_out, not_2_out, d);
  and and_18 (and_18_out, not_3_out, c);
  and and_19 (and_19_out, not_4_out, b, c);
  and and_20 (and_20_out, b, not_2_out);
  and and_21 (and_21_out, not_4_out, b, not_1_out);
  and and_22 (and_22_out, not_3_out, c);
  and and_23 (and_23_out, not_2_out, d);
  or or_1 (sa, and_1_out, and_2_out, and_3_out, and_4_out);
  or or_2 (sb, not_2_out, and_5_out, and_6_out);
  or or_3 (sc, not_3_out, and_7_out, and_8_out);
  or or_4 (sd, and_9_out, and_10_out, and_11_out, and_12_out, and_13_out);
  or or_5 (se, and_14_out, and_15_out);
  or or_6 (sf, and_16_out, and_17_out, and_18_out, and_19_out);
  or or_7 (sg, and_20_out, and_21_out, and_22_out, and_23_out);
endmodule

module ssegsim (
  input  in_1,
  input  in_2,
  input  in_3,
  input  in_4,
  input  in_5,
  input  in_6,
  input  in_7,
  input  in_8,
  input  in_9,
  output out_10
);

  wire adder4_1_s0, adder4_1_s1, adder4_1_s2, adder4_1_s3, sseg_1_sa, sseg_1_sb, sseg_1_sc, sseg_1_sd,
       sseg_1_se, sseg_1_sf, sseg_1_sg;

  adder4 adder4_1 (
    .A0(in_1), .B0(in_2), .Cin(in_3), .A1(in_4), .B1(in_5), .A2(in_6), .B2(in_7), .A3(in_8), .B3(in_9),
    .S0(adder4_1_s0), .S1(adder4_1_s1), .S2(adder4_1_s2), .S3(adder4_1_s3), .Cout(out_10));
  sseg sseg_1 (
    .d(adder4_1_s3), .c(adder4_1_s2), .b(adder4_1_s1), .a(adder4_1_s0), .sa(sseg_1_sa), .sb(sseg_1_sb),
    .sc(sseg_1_sc), .sd(sseg_1_sd), .se(sseg_1_se), .sf(sseg_1_sf), .sg(sseg_1_sg));
  _7_Segment_Display u_7_segment_display_1 (
    .g(sseg_1_sg), .f(sseg_1_sf), .a(sseg_1_sa), .b(sseg_1_sb), .e(sseg_1_se), .d(sseg_1_sd), .c(sseg_1_sc));  // open: dp
endmodule

module adder1 (
  input  A,
  input  B,
  output S,
  output C
);

  xor xor_1 (S, A, B);
  and and_1 (C, B, A);
endmodule

module adder1_full (
  input  Cin,
  input  A,
  input  B,
  output S,
  output Cout
);

  wire adder1_1_c, adder1_2_c, adder1_2_s;

  adder1 adder1_2 (.A(A), .B(B), .S(adder1_2_s), .C(adder1_2_c));
  adder1 adder1_1 (.A(Cin), .B(adder1_2_s), .S(S), .C(adder1_1_c));
  or or_1 (Cout, adder1_1_c, adder1_2_c);
endmodule

module adder4 (
  input  A0,
  input  B0,
  input  Cin,
  input  A1,
  input  B1,
  input  A2,
  input  B2,
  input  A3,
  input  B3,
  output S0,
  output S1,
  output S2,
  output S3,
  output Cout
);

  wire adder1_full_1_cout, adder1_full_2_cout, adder1_full_3_cout;

  adder1_full adder1_full_1 (.Cin(A0), .A(B0), .B(Cin), .S(S0), .Cout(adder1_full_1_cout));
  adder1_full adder1_full_2 (.Cin(adder1_full_1_cout), .A(A1), .B(B1), .S(S1), .Cout(adder1_full_2_cout));
  adder1_full adder1_full_3 (.Cin(adder1_full_2_cout), .A(A2), .B(B2), .S(S2), .Cout(adder1_full_3_cout));
  adder1_full adder1_full_4 (.Cin(adder1_full_3_cout), .A(A3), .B(B3), .S(S3), .Cout(Cout));
endmodule
