// Logisim project lab2.circ as structural Verilog: 6 circuits, main circuit main
module main (
  input  B1,
  input  B0,
  input  A1,
  input  A0,
  output D,
  output C,
  output B,
  output A
);

  wire and_2_out, and_3_out, and_4_out, and_5_out, not_1_out, not_2_out;

  not not_1 (not_1_out, B0);
  not not_2 (not_2_out, A0);
  and and_1 (D, B1, B0, A1, A0);
  and and_2 (and_2_out, B1, not_1_out, A1);
  and and_3 (and_3_out, B1, A1, not_2_out);
  and and_4 (and_4_out, B0, A1);
  and and_5 (and_5_out, B1, A0);
  and and_6 (A, B0, A0);
  or or_1 (C, and_2_out, and_3_out);
  or or_2 (B, and_4_out, and_5_out);
endmodule

module MULT2X2 (
  input  B1,
  input  B0,
  input  A1,
  input  A0,
  output D,
  output C,
  output B,
  output A
);

  wire and_2_out, and_3_out, and_4_out, and_5_out, and_6_out, and_7_out, not_1_out, not_2_out, not_3_out,
       not_4_out;

  not not_1 (not_1_out, B1);
  not not_2 (not_2_out, B0);
  not not_3 (not_3_out, A1);
  not not_4 (not_4_out, A0);
  and and_1 (D, B1, B0, A1, A0);
  and and_2 (and_2_out, B1, not_2_out, A1);
  and and_3 (and_3_out, B1, A1, not_4_out);
  and and_4 (and_4_out, not_1_out, B0, A1);
  and and_5 (and_5_out, B1, not_2_out, A0);
  and and_6 (and_6_out, B1, not_3_out, A0);
  and and_7 (and_7_out, B0, A1, not_4_out);
  and and_8 (A, B0, A0);
  or or_1 (C, and_2_out, and_3_out);
  or or_2 (B, and_4_out, and_5_out, and_6_out, and_7_out);
endmodule

module sseg (
  input  d,
  input  c,
  input  b,
  input  a,
  output sa,
  output sb,
  output sc,
  output sd,
  output se,
  output sf,
  output sg
);

  wire and_1_out, and_2_out, and_3_out, and_4_out, and_5_out, and_6_out, and_7_out, and_8_out, and_9_out,
       and_10_out, and_11_out, and_12_out, and_13_out, and_14_out, and_15_out, and_16_out, and_17_out,
       and_18_out, and_19_out, and_20_out, and_21_out, and_22_out, not_1_out, not_2_out, not_3_out, not_4_out;

  not not_1 (not_1_out, d);
  not not_2 (not_2_out, c);
  not not_3 (not_3_out, b);
  not not_4 (not_4_out, a);
  and and_1 (and_1_out, not_2_out, not_4_out);
  and and_2 (and_2_out, c, a);
  and and_3 (and_3_out, d, not_2_out);
  and and_4 (and_4_out, not_4_out, not_3_out);
  and and_5 (and_5_out, a, b, not_1_out);
  and and_6 (and_6_out, c, not_1_out);
  and and_7 (and_7_out, a, b, not_2_out);
  and and_8 (and_8_out, not_4_out, b);
  and and_9 (and_9_out, not_4_out, not_3_out, not_2_out);
  and and_10 (and_10_out, not_2_out, d);
  and and_11 (and_11_out, a, not_3_out, c);
  and and_12 (and_12_out, b, not_2_out);
  and and_13 (and_13_out, not_4_out, b);
  and and_14 (and_14_out, not_4_out, not_3_out, not_2_out);
  and and_15 (and_15_out, not_4_out, not_3_out);
  and and_16 (and_16_out, not_2_out, d);
  and and_17 (and_17_out, not_3_out, c);
  and and_18 (and_18_out, not_4_out, b, c);
  and and_19 (and_19_out, b, not_2_out);
  and and_20 (and_20_out, not_4_out, b, not_1_out);
  and and_21 (and_21_out, not_3_out, c);
  and and_22 (and_22_out, not_2_out, d);
  or or_1 (sa, and_1_out, b, and_2_out, and_3_out);
  or or_2 (sb, not_2_out, and_4_out, and_5_out);
  or or_3 (sc, not_3_out, and_6_out, and_7_out);
  or or_4 (sd, and_8_out, and_9_out, and_10_out, and_11_out, and_12_out);
  or or_5 (se, and_13_out, and_14_out);
  or or_6 (sf, and_15_out, and_16_out, and_17_out, and_18_out);
  or or_7 (sg, and_19_out, and_20_out, and_21_out, and_22_out);
endmodule

module ssegsim (
  input  in_1,
  input  in_2,
  input  in_3,
  input  in_4
);

  wire mult2x2_1_a, mult2x2_1_b, mult2x2_1_c, mult2x2_1_d, sseg_1_sa, sseg_1_sb, sseg_1_sc, sseg_1_sd,
       sseg_1_se, sseg_1_sf, sseg_1_sg;

  MULT2X2 mult2x2_1 (
    .B1(in_1), .B0(in_2), .A1(in_3), .A0(in_4), .D(mult2x2_1_d), .C(mult2x2_1_c), .B(mult2x2_1_b),
    .A(mult2x2_1_a));
  sseg sseg_1 (
    .d(mult2x2_1_d), .c(mult2x2_1_c), .b(mult2x2_1_b), .a(mult2x2_1_a), .sa(sseg_1_sa), .sb(sseg_1_sb),
    .sc(sseg_1_sc), .sd(sseg_1_sd), .se(sseg_1_se), .sf(sseg_1_sf), .sg(sseg_1_sg));
  _7_Segment_Display u_7_segment_display_1 (
    .g(sseg_1_sg), .f(sseg_1_sf), .a(sseg_1_sa), .b(sseg_1_sb), .e(sseg_1_se), .d(sseg_1_sd), .c(sseg_1_sc));  // open: dp
endmodule

module ssegbasys3 (
  input  D,
  input  C,
  input  B,
  input  A,
  output SA,
  output SB,
  output SC,
  output SD,
  output SE,
  output SF,
  output SG,
  output AN0,
  output AN1,
  output AN2,
  output AN3
);

  sseg sseg_1 (.d(D), .c(C), .b(B), .a(A), .sa(SA), .sb(SB), .sc(SC), .sd(SD), .se(SE), .sf(SF), .sg(SG));

  assign AN0 = 1'b1;
  assign AN1 = 1'b0;
  assign AN2 = 1'b0;
  assign AN3 = 1'b0;
endmodule

module MULTBASYS3 (
  input  B1,
  input  B0,
  input  A1,
  input  A0,
  output SA,
  output SB,
  output SC,
  output SD,
  output SE,
  output SF,
  output SG,
  output AN0,
  output AN1,
  output AN2,
  output AN3
);

  wire MULT2X2_1_a, MULT2X2_1_b, MULT2X2_1_c, MULT2X2_1_d;

  MULT2X2 MULT2X2_1 (
    .B1(B1), .B0(B0), .A1(A1), .A0(A0), .D(MULT2X2_1_d), .C(MULT2X2_1_c), .B(MULT2X2_1_b), .A(MULT2X2_1_a));
  sseg sseg_1 (
    .d(MULT2X2_1_d), .c(MULT2X2_1_c), .b(MULT2X2_1_b), .a(MULT2X2_1_a), .sa(SA), .sb(SB), .sc(SC), .sd(SD),
    .se(SE), .sf(SF), .sg(SG));

  assign AN0 = 1'b1;
  assign AN1 = 1'b0;
  assign AN2 = 1'b0;
  assign AN3 = 1'b0;
endmodule
