// Logisim project seq.circ as structural Verilog: 3 circuits, main circuit main
module main (
  input  in_1,
  input  clk,
  input  reset,
  output led
);

  wire next_state_1_d0, next_state_1_d1, next_state_1_d2, register_1_q, register_2_q, register_3_q;

  next_state next_state_1 (
    .q2(register_1_q), .q1(register_2_q), .q0(register_3_q), .sw(in_1), .d2(next_state_1_d2),
    .d1(next_state_1_d1), .d0(next_state_1_d0));
  Register #(.width(1)) register_1 (.D(next_state_1_d2), .clk(clk), .Q(register_1_q), .clr(reset));  // open: en
  Register #(.width(1)) register_2 (.D(next_state_1_d1), .clk(clk), .Q(register_2_q), .clr(reset));  // open: en
  Register #(.width(1)) register_3 (.D(next_state_1_d0), .clk(clk), .Q(register_3_q), .clr(reset));  // open: en
  out_logic out_logic_1 (.q2(register_1_q), .q1(register_2_q), .q0(register_3_q), .y(led));
endmodule

module next_state (
  input  q2,
  input  q1,
  input  q0,
  input  sw,
  output d2,
  output d1,
  output d0
);

  wire and_1_out, and_2_out, and_3_out, and_4_out, and_5_out, and_6_out, not_1_out, not_2_out, not_3_out;

  not not_1 (not_1_out, q2);
  not not_2 (not_2_out, q1);
  not not_3 (not_3_out, sw);
  and and_1 (and_1_out, not_1_out, q1, not_3_out);
  and and_2 (and_2_out, q2, not_2_out, not_3_out);
  and and_3 (and_3_out, q2, not_2_out, not_3_out);
  and and_4 (and_4_out, not_1_out, not_2_out, q0);
  and and_5 (and_5_out, not_1_out, q0, sw);
  and and_6 (and_6_out, q1, q0);
  or or_1 (d2, and_1_out, and_2_out);
  or or_2 (d1, and_3_out, and_4_out, and_5_out);
  or or_3 (d0, sw, and_6_out);
endmodule

module out_logic (
  input  q2,
  input  q1,
  input  q0,
  output y
);

  and and_1 (y, q2, q1);
endmodule
