// Logisim project debounce.circ as structural Verilog: 2 circuits, main circuit debounce_board
module debounce_board (
  input  reset,
  input  tl_in,
  input  clk,
  output tl_out
);

  wire comparator_1_eq, comparator_2_eq;
  wire [18:0] counter_1_q;

  Counter #(.max('h7ffff), .ongoal("stay"), .width(19)) counter_1 (
    .clr(reset), .load(1'b0), .up(tl_in), .count(1'b1), .clk(clk), .D({19{1'b0}}), .Q(counter_1_q));  // open: carry
  // Probe on counter_1_q
  Comparator #(.mode("unsigned"), .width(19)) comparator_1 (
    .a(counter_1_q), .b({19{1'b1}}), .eq(comparator_1_eq));  // open: gt, lt
  Comparator #(.mode("unsigned"), .width(19)) comparator_2 (
    .a(counter_1_q), .b({19{1'b0}}), .eq(comparator_2_eq));  // open: gt, lt
  S_R_Flip_Flop s_r_ff_1 (.S(comparator_1_eq), .R(comparator_2_eq), .clk(clk), .Q(tl_out));  // open: reset, Qn, preset

  // Notes on the sheet:
  //   Internal counter value
endmodule

module debounce_sim (
  input  reset,
  input  tl_in,
  input  clk,
  output tl_out
);

  wire comparator_1_eq, comparator_2_eq;
  wire [2:0] counter_1_q;

  Counter #(.max('h7), .ongoal("stay"), .width(3)) counter_1 (
    .clr(reset), .load(1'b0), .up(tl_in), .count(1'b1), .clk(clk), .D(3'b000), .Q(counter_1_q));  // open: carry
  // Probe on counter_1_q
  Comparator #(.mode("unsigned"), .width(3)) comparator_1 (
    .a(counter_1_q), .b(3'b111), .eq(comparator_1_eq));  // open: gt, lt
  Comparator #(.mode("unsigned"), .width(3)) comparator_2 (
    .a(counter_1_q), .b(3'b000), .eq(comparator_2_eq));  // open: gt, lt
  S_R_Flip_Flop s_r_ff_1 (.S(comparator_1_eq), .R(comparator_2_eq), .clk(clk), .Q(tl_out));  // open: reset, Qn, preset

  // Notes on the sheet:
  //   Internal counter value
endmodule
