// Logisim project fin.circ as structural Verilog: 8 circuits, main circuit main
module main (
  input  roll,
  input  reset
);

  wire clk_out, controler_1_ce, controler_1_si, counter_1_carry, debounce_board_1_tl_out;
  wire [3:0] ShiftReg_1_a;

  Clock clk (.out(clk_out));
  Counter #(.max('hffffff), .width(24)) counter_1 (
    .clr(reset), .count(controler_1_ce), .clk(clk_out), .carry(counter_1_carry));  // open: load, up, D, Q
  debounce_board debounce_board_1 (.reset(reset), .tl_in(roll), .clk(clk_out), .tl_out(debounce_board_1_tl_out));
  controler controler_1 (
    .r(debounce_board_1_tl_out), .s(counter_1_carry), .clk(clk_out), .reset(reset), .ce(controler_1_ce),
    .si(controler_1_si));
  ShiftReg ShiftReg_1 (
    .shift_in(controler_1_si), .count(counter_1_carry), .clk(clk_out), .reset(reset), .a(ShiftReg_1_a[0]),
    .b(ShiftReg_1_a[1]), .c(ShiftReg_1_a[2]), .d(ShiftReg_1_a[3]));
  Hex_Digit_Display #(.decimalPoint("false")) Hex_Digit_Display_1 (.value(ShiftReg_1_a));
endmodule

module debounce_board (
  input  reset,
  input  tl_in,
  input  clk,
  output tl_out
);

  wire comparator_1_eq, comparator_2_eq;
  wire [18:0] counter_1_q;

  Counter #(.max('h7ffff), .ongoal("stay"), .width(19)) counter_1 (
    .clr(reset), .load(1'b0), .up(tl_in), .count(1'b1), .clk(clk), .D({19{1'b0}}), .Q(counter_1_q));  // open: carry
  // Probe on counter_1_q
  Comparator #(.mode("unsigned"), .width(19)) comparator_1 (
    .a(counter_1_q), .b({19{1'b1}}), .eq(comparator_1_eq));  // open: gt, lt
  Comparator #(.mode("unsigned"), .width(19)) comparator_2 (
    .a(counter_1_q), .b({19{1'b0}}), .eq(comparator_2_eq));  // open: gt, lt
  S_R_Flip_Flop s_r_ff_1 (.S(comparator_1_eq), .R(comparator_2_eq), .clk(clk), .Q(tl_out));  // open: reset, Qn, preset

  // Notes on the sheet:
  //   Internal counter value
endmodule

module debounce_sim (
  input  reset,
  input  tl_in,
  input  clk,
  output tl_out
);

  wire comparator_1_eq, comparator_2_eq;
  wire [2:0] counter_1_q;

  Counter #(.max('h7), .ongoal("stay"), .width(3)) counter_1 (
    .clr(reset), .load(1'b0), .up(tl_in), .count(1'b1), .clk(clk), .D(3'b000), .Q(counter_1_q));  // open: carry
  // Probe on counter_1_q
  Comparator #(.mode("unsigned"), .width(3)) comparator_1 (
    .a(counter_1_q), .b(3'b111), .eq(comparator_1_eq));  // open: gt, lt
  Comparator #(.mode("unsigned"), .width(3)) comparator_2 (
    .a(counter_1_q), .b(3'b000), .eq(comparator_2_eq));  // open: gt, lt
  S_R_Flip_Flop s_r_ff_1 (.S(comparator_1_eq), .R(comparator_2_eq), .clk(clk), .Q(tl_out));  // open: reset, Qn, preset

  // Notes on the sheet:
  //   Internal counter value
endmodule

module Main_sim (
  input  roll,
  input  in_2
);

  wire clock_1_out, controler_1_ce, controler_1_si, counter_1_carry, debounce_sim_1_tl_out;
  wire [3:0] shiftreg_1_a;

  Clock clock_1 (.out(clock_1_out));
  Counter #(.max('hf), .width(4)) counter_1 (
    .clr(in_2), .count(controler_1_ce), .clk(clock_1_out), .carry(counter_1_carry));  // open: load, up, D, Q
  debounce_sim debounce_sim_1 (.reset(in_2), .tl_in(roll), .clk(clock_1_out), .tl_out(debounce_sim_1_tl_out));
  controler controler_1 (
    .r(debounce_sim_1_tl_out), .s(counter_1_carry), .clk(clock_1_out), .reset(in_2), .ce(controler_1_ce),
    .si(controler_1_si));
  ShiftReg shiftreg_1 (
    .shift_in(controler_1_si), .count(counter_1_carry), .clk(clock_1_out), .reset(in_2), .a(shiftreg_1_a[0]),
    .b(shiftreg_1_a[1]), .c(shiftreg_1_a[2]), .d(shiftreg_1_a[3]));
  Hex_Digit_Display #(.decimalPoint("false")) hex_digit_display_1 (.value(shiftreg_1_a));
endmodule

module ShiftReg (
  input  shift_in,
  input  count,
  input  clk,
  input  reset,
  output a,
  output b,
  output c,
  output d
);

  wire or_1_out, xor_1_out;

  xor xor_1 (xor_1_out, d, c);
  or or_1 (or_1_out, xor_1_out, shift_in);
  Register #(.width(1)) register_1 (.D(or_1_out), .en(count), .clk(clk), .Q(a), .clr(reset));
  Register #(.width(1)) register_2 (.D(a), .en(count), .clk(clk), .Q(b), .clr(reset));
  Register #(.width(1)) register_3 (.D(b), .en(count), .clk(clk), .Q(c), .clr(reset));
  Register #(.width(1)) register_4 (.D(c), .en(count), .clk(clk), .Q(d), .clr(reset));
endmodule

module controler (
  input  r,
  input  s,
  input  clk,
  input  reset,
  output ce,
  output si
);

  wire next_state_logic_1_d0, next_state_logic_1_d1, register_1_q, register_2_q;

  next_state_logic next_state_logic_1 (
    .r(r), .s(s), .q1(register_1_q), .q0(register_2_q), .d1(next_state_logic_1_d1), .d0(next_state_logic_1_d0));
  Register #(.width(1)) register_1 (.D(next_state_logic_1_d1), .clk(clk), .Q(register_1_q), .clr(reset));  // open: en
  Register #(.width(1)) register_2 (.D(next_state_logic_1_d0), .clk(clk), .Q(register_2_q), .clr(reset));  // open: en
  out_logic out_logic_1 (.d1(register_1_q), .d0(register_2_q), .ce(ce), .si(si));
endmodule

module next_state_logic (
  input  r,
  input  s,
  input  q1,
  input  q0,
  output d1,
  output d0
);

  wire and_1_out, and_2_out, and_3_out, and_4_out, and_5_out, and_6_out, not_1_out, not_2_out, not_3_out;

  not not_1 (not_1_out, r);
  not not_2 (not_2_out, s);
  not not_3 (not_3_out, q1);
  and and_1 (and_1_out, not_1_out, s, q0);
  and and_2 (and_2_out, not_2_out, q0);
  and and_3 (and_3_out, q1, q0);
  and and_4 (and_4_out, r, not_2_out, not_3_out);
  and and_5 (and_5_out, r, q0);
  and and_6 (and_6_out, r, s, q1);
  or or_1 (d1, q1, and_1_out);
  or or_2 (d0, and_2_out, and_3_out, and_4_out, and_5_out, and_6_out);
endmodule

module out_logic (
  input  d1,
  input  d0,
  output ce,
  output si
);

  wire and_1_out, and_2_out, not_1_out, not_2_out;

  not not_1 (not_1_out, d1);
  not not_2 (not_2_out, d0);
  and and_1 (and_1_out, not_1_out, d0);
  and and_2 (and_2_out, d1, not_2_out);
  or or_1 (ce, and_1_out, and_2_out);

  assign si = d0;
endmodule
